# Fritzing sketch five_red_leds (saved by Fritzing 0.9.3b)
breadboards: 1

parts:
  LED1 = LED - 5mm [color="Red (633nm)" package="5 mm [THT]"]
  LED2 = LED - 5mm [color="Red (633nm)" package="5 mm [THT]"]
  LED3 = LED - 5mm [color="Red (633nm)" package="5 mm [THT]"]
  LED4 = LED - 5mm [color="Red (633nm)" package="5 mm [THT]"]
  LED5 = LED - 5mm [color="Red (633nm)" package="5 mm [THT]"]
  R1 = Resistor [tolerance=±5% resistance=330 package=THT]
  R2 = Resistor [tolerance=±5% resistance=330 package=THT]
  R3 = Resistor [tolerance=±5% resistance=330 package=THT]
  R4 = Resistor [tolerance=±5% resistance=330 package=THT]
  R5 = Resistor [tolerance=±5% resistance=330 package=THT]
  Composant1 = Arduino Mega 2560 (Rev3)

nets:
  N1: LED1.cathode, R5.Pin_1
  N2: LED1.anode, Composant1.D39
  N3: LED2.cathode, R4.Pin_1
  N4: LED2.anode, Composant1.D37
  N5: LED3.cathode, R3.Pin_1
  N6: LED3.anode, Composant1.D35
  N7: LED4.cathode, R2.Pin_1
  N8: LED4.anode, Composant1.D33
  N9: LED5.cathode, R1.Pin_1
  N10: LED5.anode, Composant1.D31
  N11: R1.Pin_0, R2.Pin_0, R3.Pin_0, R4.Pin_0, R5.Pin_0, Composant1.GND
