# Fritzing sketch ultra_distance (saved by Fritzing 0.9.3b)
breadboards: 1

parts:
  Grove1 = Grove 4 Digit Display
  HC-SR04_Sensor_1 = HC-SR04 Ultrasonic Distance Sensor
  Composant1 = Arduino Mega 2560 (Rev3)

nets:
  GND: Grove1.GND, HC-SR04_Sensor_1.GND, Composant1.GND
  VCC: Grove1.VCC, HC-SR04_Sensor_1.VCC, Composant1.5V
  N1: Grove1.DIO, Composant1.D3_PWM
  N2: Grove1.CLK, Composant1.D2_PWM
  N3: HC-SR04_Sensor_1.TRIG, Composant1.D30
  N4: HC-SR04_Sensor_1.ECHO, Composant1.D32
